# Fritzing sketch QuikBrew_Mega (saved by Fritzing 0.7.0b)
breadboards: 1

parts:
  R1 = Resistor [tolerance=±5% resistance=220 package=THT]
  Relay_3 = mystery part, 3 pins [chip_label=Relay spacing=300mil]
  Relay_2 = mystery part, 3 pins [chip_label=Relay spacing=300mil]
  Relay_2_LED = LED - 5mm [color="Red (633nm)" package="5 mm [THT]"]
  R2 = Resistor [tolerance=±5% resistance=4.7 package=THT]
  Temp_2 = mystery part, 3 pins [chip_label=Temp spacing=300mil]
  Temp_1 = mystery part, 3 pins [chip_label=Temp spacing=300mil]
  R3 = Resistor [tolerance=±5% resistance=220 package=THT]
  Ready_LED = LED - 5mm [color="Green (570nm)" package="5 mm [THT]"]
  Button_2 = Round Pushbutton
  Button_1 = Round Pushbutton
  R4 = Resistor [tolerance=±5% resistance=10k package=THT]
  R5 = Resistor [tolerance=±5% resistance=10k package=THT]
  Relay_1 = mystery part, 3 pins [chip_label=Relay spacing=300mil]
  R6 = Resistor [tolerance=±5% resistance=220 package=THT]
  Relay1_LED = LED - 5mm [color="Red (633nm)" package="5 mm [THT]"]
  LCD = mystery part, 4 pins [chip_label="LCD 4x20" spacing=300mil]
  U1 = Arduino Mega
  SD_Card_Reader = mystery part, 6 pins [chip_label="SD Card" spacing=300mil]

nets:
  N1: R1.Pin_0, Relay_2.pin2, U1.D38
  N2: R1.Pin_1, Relay_2_LED.anode
  N3: Relay_3.pin2, U1.D40
  N4: Relay_2_LED.cathode, Temp_2.pin1, Temp_1.pin1, Ready_LED.anode, Button_2.leg1, Button_1.leg1, LCD.pin2
  N5: R2.Pin_0, Temp_2.pin2, Temp_1.pin2, U1.D36
  N6: R2.Pin_1, Temp_2.pin3, Temp_1.pin3, R4.Pin_1, R5.Pin_1, LCD.pin1
  N7: R3.Pin_0, U1.D34
  N8: R3.Pin_1, Ready_LED.cathode
  N9: Button_2.leg0, R5.Pin_0, U1.D32
  N10: Button_1.leg0, R4.Pin_0, U1.D30
  N11: Relay_1.pin2, R6.Pin_0, U1.D28
  N12: R6.Pin_1, Relay1_LED.anode
  N13: Relay1_LED.cathode, U1.GND, SD_Card_Reader.pin1
  N14: LCD.pin3, U1.D20
  N15: LCD.pin4, U1.D21
  N16: U1.+5V, SD_Card_Reader.pin2
  N17: U1.D50, SD_Card_Reader.pin3
  N18: U1.D51, SD_Card_Reader.pin4
  N19: U1.D52, SD_Card_Reader.pin6
  N20: U1.D53, SD_Card_Reader.pin5
